// Logisim project Computer.circ as structural Verilog: 9 circuits, main circuit main
module main (
);

  wire adder_1_cout, CE, Clear_out, CLK, clock_1_out, CO, comparator_1_eq, comparator_1_gt, comparator_1_lt,
       instruction_decoder_1_ai, instruction_decoder_1_ao, instruction_decoder_1_bi,
       instruction_decoder_1_bo, instruction_decoder_1_fi, instruction_decoder_1_hlt,
       instruction_decoder_1_ii, instruction_decoder_1_io, instruction_decoder_1_mi,
       instruction_decoder_1_oi, instruction_decoder_1_re, instruction_decoder_1_ri,
       instruction_decoder_1_ro, instruction_decoder_1_sc, instruction_decoder_1_sho,
       instruction_decoder_1_sw, J, or_1_out, RST, RUN, SO, SU, subtractor_1_bout;
  wire [3:0] bitselector_1_out, bitselector_2_out, bitselector_3_out, bitselector_4_out, bitselector_5_out,
       bitselector_6_out;
  wire [6:0] keyboard_1_data;
  wire [15:0] A_q, adder_1_out, B_q, flag_bits_handler_1_out_6, FLAGS, IR_q, lsb_sel_1_out_2,
       lsb_sel_2_out_2, MAR_q, n4_4bit_combiner_1_out_4, OUT, PC_q, ram_1_data, shifter_1_out, STEP_q,
       subtractor_1_out;
  wire [19:0] rom_1_data;
  wire [20:0] rom_2_data;

  LSB_sel lsb_sel_1 (.in_1(ram_1_data), .out_2(lsb_sel_1_out_2));
  Counter #(.width(16), .max('h4)) STEP (.Q(STEP_q), .clk(CLK), .clr(RST));  // open: load, D, count, carry
  Clock clock_1 (.out(clock_1_out));
  Hex_Digit_Display hex_digit_display_1 (.value(bitselector_1_out));  // open: dp
  Hex_Digit_Display hex_digit_display_2 (.value(bitselector_2_out));  // open: dp
  BitSelector #(.width(20), .group(4)) bitselector_1 (.in(rom_1_data), .out(bitselector_1_out), .sel(3'b100));
  Register #(.width(16)) MAR (.D(lsb_sel_1_out_2), .en(instruction_decoder_1_mi), .Q(MAR_q), .clk(CLK), .clr(RST));
  or or_1 (or_1_out, instruction_decoder_1_ro, instruction_decoder_1_ri);
  HaltController haltcontroller_1 (.CLK(clock_1_out), .HLT(instruction_decoder_1_hlt), .Run(RUN), .K(CLK));
  Hex_Digit_Display hex_digit_display_3 (.value(bitselector_4_out));  // open: dp
  Hex_Digit_Display hex_digit_display_4 (.value(bitselector_3_out));  // open: dp
  BitSelector #(.width(20), .group(4)) bitselector_2 (.in(rom_1_data), .out(bitselector_2_out), .sel(3'b011));
  ROM #(.addrWidth(16), .dataWidth(20)) rom_1 (.addr(OUT), .data(rom_1_data));  // open: sel
  _4_4bit_combiner u_4_4bit_combiner_1 (
    .FLAGS(FLAGS), .STEP(STEP_q), .INSTRUCTION(IR_q), .out_4(n4_4bit_combiner_1_out_4));
  Instruction_Decoder instruction_decoder_1 (
    .in_1(rom_2_data), .HLT(instruction_decoder_1_hlt), .MI(instruction_decoder_1_mi),
    .RI(instruction_decoder_1_ri), .RO(instruction_decoder_1_ro), .IO(instruction_decoder_1_io),
    .II(instruction_decoder_1_ii), .AI(instruction_decoder_1_ai), .AO(instruction_decoder_1_ao), .SO(SO),
    .SU(SU), .BI(instruction_decoder_1_bi), .BO(instruction_decoder_1_bo), .CE(CE), .CO(CO), .J(J),
    .FI(instruction_decoder_1_fi), .ShO(instruction_decoder_1_sho), .SW(instruction_decoder_1_sw),
    .SC(instruction_decoder_1_sc), .RE(instruction_decoder_1_re), .OI(instruction_decoder_1_oi));
  Hex_Digit_Display hex_digit_display_5 (.value(bitselector_5_out));  // open: dp
  BitSelector #(.width(20), .group(4)) bitselector_3 (.in(rom_1_data), .out(bitselector_3_out), .sel(3'b010));
  BitSelector #(.width(20), .group(4)) bitselector_4 (.in(rom_1_data), .out(bitselector_4_out), .sel(3'b001));
  RAM #(.addrWidth(16), .dataWidth(16)) ram_1 (
    .addr(MAR_q), .data(ram_1_data), .sel(or_1_out), .clk(CLK), .ld(instruction_decoder_1_ro));  // open: clr
  assign ram_1_data = CO ? PC_q : 16'bz;  // Controlled_Buffer controlled_buffer_1
  Counter #(.width(16), .max('hffff)) PC (
    .load(J), .D(lsb_sel_2_out_2), .count(CE), .Q(PC_q), .clk(CLK), .clr(RST));  // open: carry
  assign ram_1_data = instruction_decoder_1_io ? IR_q : 16'bz;  // Controlled_Buffer controlled_buffer_2
  Register #(.width(16)) IR (.D(ram_1_data), .en(instruction_decoder_1_ii), .Q(IR_q), .clk(CLK), .clr(RST));
  BitSelector #(.width(20), .group(4)) bitselector_5 (.in(rom_1_data), .out(bitselector_5_out), .sel(3'b000));
  Pull_Resistor pull_resistor_1 (.node(ram_1_data));
  LSB_sel lsb_sel_2 (.in_1(ram_1_data), .out_2(lsb_sel_2_out_2));
  ROM #(.addrWidth(16), .dataWidth(21)) rom_2 (.addr(n4_4bit_combiner_1_out_4), .data(rom_2_data));  // open: sel
  assign ram_1_data = instruction_decoder_1_sho ? shifter_1_out : 16'bz;  // Controlled_Buffer controlled_buffer_3
  assign ram_1_data = instruction_decoder_1_ao ? A_q : 16'bz;  // Controlled_Buffer controlled_buffer_4
  assign ram_1_data = instruction_decoder_1_bo ? B_q : 16'bz;  // Controlled_Buffer controlled_buffer_5
  assign ram_1_data = SO ? adder_1_out : 16'bz;  // Controlled_Buffer controlled_buffer_6
  assign ram_1_data = SU ? subtractor_1_out : 16'bz;  // Controlled_Buffer controlled_buffer_7
  TTY tty_1 (.data(ram_1_data[6:0]), .clk(CLK), .we(instruction_decoder_1_sw), .clr(instruction_decoder_1_sc));
  assign ram_1_data[6:0] = instruction_decoder_1_re ? keyboard_1_data : 7'bz;  // Controlled_Buffer controlled_buffer_8
  Shifter #(.width(16)) shifter_1 (.in(A_q), .\dist (bitselector_6_out), .out(shifter_1_out));
  Register #(.width(16)) A (.D(ram_1_data), .en(instruction_decoder_1_ai), .Q(A_q), .clk(CLK), .clr(RST));
  Register #(.width(16)) B (.D(ram_1_data), .en(instruction_decoder_1_bi), .Q(B_q), .clk(CLK), .clr(RST));
  BitSelector #(.width(16), .group(4)) bitselector_6 (.in(B_q), .out(bitselector_6_out), .sel(2'b00));
  Adder #(.width(16)) adder_1 (.a(A_q), .b(B_q), .out(adder_1_out), .cout(adder_1_cout));  // open: cin
  Subtractor #(.width(16)) subtractor_1 (
    .a(A_q), .b(B_q), .out(subtractor_1_out), .bout(subtractor_1_bout));  // open: bin
  Comparator #(.width(16), .mode("unsigned")) comparator_1 (
    .a(A_q), .b(B_q), .gt(comparator_1_gt), .eq(comparator_1_eq), .lt(comparator_1_lt));
  Register #(.width(16)) u_OUT (.D(ram_1_data), .en(instruction_decoder_1_oi), .Q(OUT), .clk(CLK));  // open: clr
  DotMatrix #(.matrixcols(16), .matrixrows(1)) dotmatrix_1 (
    .col0(ram_1_data[15]), .col1(ram_1_data[14]), .col2(ram_1_data[13]), .col3(ram_1_data[12]),
    .col4(ram_1_data[11]), .col5(ram_1_data[10]), .col6(ram_1_data[9]), .col7(ram_1_data[8]),
    .col8(ram_1_data[7]), .col9(ram_1_data[6]), .col10(ram_1_data[5]), .col11(ram_1_data[4]),
    .col12(ram_1_data[3]), .col13(ram_1_data[2]), .col14(ram_1_data[1]), .col15(ram_1_data[0]));
  Keyboard keyboard_1 (
    .clk(CLK), .re(instruction_decoder_1_re), .clr(Clear_out), .data(keyboard_1_data));  // open: avail
  flag_bits_handler flag_bits_handler_1 (
    .CARRY(adder_1_cout), .BORROW(subtractor_1_bout), .EQUALS(comparator_1_eq), .GREATER(comparator_1_gt),
    .LESS(comparator_1_lt), .out_6(flag_bits_handler_1_out_6));
  Register #(.width(16)) u_FLAGS (
    .D(flag_bits_handler_1_out_6), .en(instruction_decoder_1_fi), .Q(FLAGS), .clk(CLK), .clr(RST));
  Button Clear (.out(Clear_out));
  Button u_Run (.out(RUN));
  Button Reset (.out(RST));

  // Notes on the sheet:
  //   7-Segment Decoder
  //   contents of rom_1 (hex, n*v repeats v):
  //   0 1 2 3 4 5 6 7 8 9 10 11 12 13 14 15 16 17 18 19 20 21 22 23 24 25 26 27 28 29 30 31 32 33 34 35 36
  //   37 38 39 40 41 42 43 44 45 46 47 48 49 50 51 52 53 54 55 56 57 58 59 60 61 62 63 64 65 66 67 68 69
  //   70 71 72 73 74 75 76 77 78 79 80 81 82 83 84 85 86 87 88 89 90 91 92 93 94 95 96 97 98 99 100 101
  //   102 103 104 105 106 107 108 109 110 111 112 113 114 115 116 117 118 119 120 121 122 123 124 125 126
  //   127 128 129 130 131 132 133 134 135 136 137 138 139 140 141 142 143 144 145 146 147 148 149 150 151
  //   152 153 154 155 156 157 158 159 160 161 162 163 164 165 166 167 168 169 170 171 172 173 174 175 176
  //   177 178 179 180 181 182 183 184 185 186 187 188 189 190 191 192 193 194 195 196 197 198 199 200 201
  //   202 203 204 205 206 207 208 209 210 211 212 213 214 215 216 217 218 219 220 221 222 223 224 225 226
  //   227 228 229 230 231 232 233 234 235 236 237 238 239 240 241 242 243 244 245 246 247 248 249 250 251
  //   252 253 254 255 256 257 258 259 260 261 262 263 264 265 266 267 268 269 270 271 272 273 274 275 276
  //   277 278 279 280 281 282 283 284 285 286 287 288 289 290 291 292 293 294 295 296 297 298 299 300 301
  //   302 303 304 305 306 307 308 309 310 311 312 313 314 315 316 317 318 319 320 321 322 323 324 325 326
  //   327 328 329 330 331 332 333 334 335 336 337 338 339 340 341 342 343 344 345 346 347 348 349 350 351
  //   352 353 354 355 356 357 358 359 360 361 362 363 364 365 366 367 368 369 370 371 372 373 374 375 376
  //   377 378 379 380 381 382 383 384 385 386 387 388 389 390 391 392 393 394 395 396 397 398 399 400 401
  //   402 403 404 405 406 407 408 409 410 411 412 413 414 415 416 417 418 419 420 421 422 423 424 425 426
  //   427 428 429 430 431 432 433 434 435 436 437 438 439 440 441 442 443 444 445 446 447 448 449 450 451
  //   452 453 454 455 456 457 458 459 460 461 462 463 464 465 466 467 468 469 470 471 472 473 474 475 476
  //   477 478 479 480 481 482 483 484 485 486 487 488 489 490 491 492 493 494 495 496 497 498 499 500 501
  //   502 503 504 505 506 507 508 509 510 511 512 513 514 515 516 517 518 519 520 521 522 523 524 525 526
  //   527 528 529 530 531 532 533 534 535 536 537 538 539 540 541 542 543 544 545 546 547 548 549 550 551
  //   552 553 554 555 556 557 558 559 560 561 562 563 564 565 566 567 568 569 570 571 572 573 574 575 576
  //   577 578 579 580 581 582 583 584 585 586 587 588 589 590 591 592 593 594 595 596 597 598 599 600 601
  //   602 603 604 605 606 607 608 609 610 611 612 613 614 615 616 617 618 619 620 621 622 623 624 625 626
  //   627 628 629 630 631 632 633 634 635 636 637 638 639 640 641 642 643 644 645 646 647 648 649 650 651
  //   652 653 654 655 656 657 658 659 660 661 662 663 664 665 666 667 668 669 670 671 672 673 674 675 676
  //   677 678 679 680 681 682 683 684 685 686 687 688 689 690 691 692 693 694 695 696 697 698 699 700 701
  //   702 703 704 705 706 707 708 709 710 711 712 713 714 715 716 717 718 719 720 721 722 723 724 725 726
  //   727 728 729 730 731 732 733 734 735 736 737 738 739 740 741 742 743 744 745 746 747 748 749 750 751
  //   752 753 754 755 756 757 758 759 760 761 762 763 764 765 766 767 768 769 770 771 772 773 774 775 776
  //   777 778 779 780 781 782 783 784 785 786 787 788 789 790 791 792 793 794 795 796 797 798 799 800 801
  //   802 803 804 805 806 807 808 809 810 811 812 813 814 815 816 817 818 819 820 821 822 823 824 825 826
  //   827 828 829 830 831 832 833 834 835 836 837 838 839 840 841 842 843 844 845 846 847 848 849 850 851
  //   852 853 854 855 856 857 858 859 860 861 862 863 864 865 866 867 868 869 870 871 872 873 874 875 876
  //   877 878 879 880 881 882 883 884 885 886 887 888 889 890 891 892 893 894 895 896 897 898 899 900 901
  //   902 903 904 905 906 907 908 909 910 911 912 913 914 915 916 917 918 919 920 921 922 923 924 925 926
  //   927 928 929 930 931 932 933 934 935 936 937 938 939 940 941 942 943 944 945 946 947 948 949 950 951
  //   952 953 954 955 956 957 958 959 960 961 962 963 964 965 966 967 968 969 970 971 972 973 974 975 976
  //   977 978 979 980 981 982 983 984 985 986 987 988 989 990 991 992 993 994 995 996 997 998 999 1000
  //   1001 1002 1003 1004 1005 1006 1007 1008 1009 1010 1011 1012 1013 1014 1015 1016 1017 1018 1019 1020
  //   1021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
  //   System RAM
  //   Instruction Decoder
  //   contents of rom_2 (hex, n*v repeats v):
  //   32*80080 32*28100 192*0 32*80080 32*28100 32*90000 32*24000 128*0 32*80080 32*28100 32*90000
  //   32*42000 128*0 32*80080 32*28100 32*14000 160*0 32*80080 32*28100 32*90000 32*20400 32*5020 96*0
  //   32*80080 32*28100 32*90000 32*20400 32*4820 96*0 32*80080 32*28100 32*90000 32*20040 128*0 32*80080
  //   32*28100 32*90000 4*0 4*20040 4*0 4*20040 4*0 4*20040 4*0 4*20040 128*0 32*80080 32*28100 32*90000
  //   32*20400 32*20 96*0 32*80080 32*28100 32*90000 8*0 8*20040 8*0 8*20040 128*0 32*80080 32*28100
  //   32*90000 16*0 16*20040 128*0 32*80080 32*28100 32*80200 32*24000 128*0 32*80080 32*28100 32*80200
  //   32*42000 128*0 32*80080 32*28100 32*90000 32*20400 128*0 32*80080 32*28100 32*90000 32*40200 128*0
  //   32*80080 32*28100 32*90000 32*20400 32*4010 96*0 32*80080 32*28100 32*4002 160*0 32*80080 32*28100
  //   32*2008 160*0 32*80080 32*28100 32*4 160*0 32*80080 32*28100 32*2001 160*0 32*80080 32*28100
  //   32*90000 0 20040 0 20040 0 20040 0 20040 0 20040 0 20040 0 20040 0 20040 0 20040 0 20040 0 20040 0
  //   20040 0 20040 0 20040 0 20040 0 20040 128*0 32*80080 32*28100 192*0 32*80080 32*28100 192*0 32*80080
  //   32*28100 192*0 32*80080 32*28100 192*0 32*80080 32*28100 192*0 32*80080 32*28100 192*0 32*80080
  //   32*28100 192*0 32*80080 32*28100 192*0 32*80080 32*28100 192*0 32*80080 32*28100 192*0 32*80080
  //   32*28100 192*0 32*80080 32*28100 192*0 32*80080 32*28100 192*0 32*80080 32*28100 192*0 32*80080
  //   32*28100 192*0 32*80080 32*28100 192*0 32*80080 32*28100 192*0 32*80080 32*28100 192*0 32*80080
  //   32*28100 192*0 32*80080 32*28100 192*0 32*80080 32*28100 192*0 32*80080 32*28100 192*0 32*80080
  //   32*28100 192*0 32*80080 32*28100 192*0 32*80080 32*28100 192*0 32*80080 32*28100 192*0 32*80080
  //   32*28100 192*0 32*80080 32*28100 192*0 32*80080 32*28100 192*0 32*80080 32*28100 192*0 32*80080
  //   32*28100 192*0 32*80080 32*28100 192*0 32*80080 32*28100 192*0 32*80080 32*28100 192*0 32*80080
  //   32*28100 192*0 32*80080 32*28100 192*0 32*80080 32*28100 192*0 32*80080 32*28100 192*0 32*80080
  //   32*28100 192*0 32*80080 32*28100 192*0 32*80080 32*28100 192*0 32*80080 32*28100 192*0 32*80080
  //   32*28100 192*0 32*80080 32*28100 192*0 32*80080 32*28100 192*0 32*80080 32*28100 192*0 32*80080
  //   32*28100 192*0 32*80080 32*28100 192*0 32*80080 32*28100 192*0 32*80080 32*28100 192*0 32*80080
  //   32*28100 192*0 32*80080 32*28100 192*0 32*80080 32*28100 192*0 32*80080 32*28100 192*0 32*80080
  //   32*28100 192*0 32*80080 32*28100 192*0 32*80080 32*28100 192*0 32*80080 32*28100 192*0 32*80080
  //   32*28100 192*0 32*80080 32*28100 192*0 32*80080 32*28100 192*0 32*80080 32*28100 192*0 32*80080
  //   32*28100 192*0 32*80080 32*28100 192*0 32*80080 32*28100 192*0 32*80080 32*28100 192*0 32*80080
  //   32*28100 192*0 32*80080 32*28100 192*0 32*80080 32*28100 192*0 32*80080 32*28100 192*0 32*80080
  //   32*28100 192*0 32*80080 32*28100 192*0 32*80080 32*28100 192*0 32*80080 32*28100 192*0 32*80080
  //   32*28100 192*0 32*80080 32*28100 192*0 32*80080 32*28100 192*0 32*80080 32*28100 192*0 32*80080
  //   32*28100 192*0 32*80080 32*28100 192*0 32*80080 32*28100 192*0 32*80080 32*28100 192*0 32*80080
  //   32*28100 192*0 32*80080 32*28100 192*0 32*80080 32*28100 192*0 32*80080 32*28100 192*0 32*80080
  //   32*28100 192*0 32*80080 32*28100 192*0 32*80080 32*28100 192*0 32*80080 32*28100 192*0 32*80080
  //   32*28100 192*0 32*80080 32*28100 192*0 32*80080 32*28100 192*0 32*80080 32*28100 192*0 32*80080
  //   32*28100 192*0 32*80080 32*28100 192*0 32*80080 32*28100 192*0 32*80080 32*28100 192*0 32*80080
  //   32*28100 192*0 32*80080 32*28100 192*0 32*80080 32*28100 192*0 32*80080 32*28100 192*0 32*80080
  //   32*28100 192*0 32*80080 32*28100 192*0 32*80080 32*28100 192*0 32*80080 32*28100 192*0 32*80080
  //   32*28100 192*0 32*80080 32*28100 192*0 32*80080 32*28100 192*0 32*80080 32*28100 192*0 32*80080
  //   32*28100 192*0 32*80080 32*28100 192*0 32*80080 32*28100 192*0 32*80080 32*28100 192*0 32*80080
  //   32*28100 192*0 32*80080 32*28100 192*0 32*80080 32*28100 192*0 32*80080 32*28100 192*0 32*80080
  //   32*28100 192*0 32*80080 32*28100 192*0 32*80080 32*28100 192*0 32*80080 32*28100 192*0 32*80080
  //   32*28100 192*0 32*80080 32*28100 192*0 32*80080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
  //   Bus Signals
endmodule

module ram (
  output [3:0] out_1,
  output [3:0] out_2,
  output [3:0] out_3,
  output [3:0] out_4,
  output [3:0] out_5
);

  wire [15:0] undriven;
  wire [19:0] rom_1_data;

  ROM #(.addrWidth(16), .dataWidth(20)) rom_1 (.addr(undriven), .data(rom_1_data));  // open: sel
  BitSelector #(.width(20), .group(4)) bitselector_1 (.in(rom_1_data), .out(out_1), .sel(3'b100));
  BitSelector #(.width(20), .group(4)) bitselector_2 (.in(rom_1_data), .out(out_2), .sel(3'b011));
  BitSelector #(.width(20), .group(4)) bitselector_3 (.in(rom_1_data), .out(out_3), .sel(3'b010));
  BitSelector #(.width(20), .group(4)) bitselector_4 (.in(rom_1_data), .out(out_4), .sel(3'b001));
  BitSelector #(.width(20), .group(4)) bitselector_5 (.in(rom_1_data), .out(out_5), .sel(3'b000));
endmodule

module _4_4bit_combiner (
  input  [15:0] FLAGS,
  input  [15:0] STEP,
  input  [15:0] INSTRUCTION,
  output [15:0] out_4
);


  assign out_4 = {INSTRUCTION[15:8], STEP[2:0], FLAGS[4:0]};
endmodule

module Instruction_Decoder (
  input  [20:0] in_1,
  output HLT,
  output MI,
  output RI,
  output RO,
  output IO,
  output II,
  output AI,
  output AO,
  output SO,
  output SU,
  output BI,
  output BO,
  output CE,
  output CO,
  output J,
  output FI,
  output ShO,
  output SW,
  output SC,
  output RE,
  output OI
);


  assign AI = in_1[14];
  assign AO = in_1[13];
  assign BI = in_1[10];
  assign BO = in_1[9];
  assign CE = in_1[8];
  assign CO = in_1[7];
  assign FI = in_1[5];
  assign HLT = in_1[20];
  assign II = in_1[15];
  assign IO = in_1[16];
  assign J = in_1[6];
  assign MI = in_1[19];
  assign OI = in_1[0];
  assign RE = in_1[1];
  assign RI = in_1[18];
  assign RO = in_1[17];
  assign SC = in_1[2];
  assign ShO = in_1[4];
  assign SO = in_1[12];
  assign SU = in_1[11];
  assign SW = in_1[3];
endmodule

module LSB_sel (
  input  [15:0] in_1,
  output [15:0] out_2
);


  assign out_2 = {{8{1'b0}}, in_1[7:0]};
endmodule

module _3display_splitter (
  input  [7:0] in_1,
  input  [7:0] in_2,
  input  in_3,
  output [11:0] out_4,
  output [11:0] out_5
);

  wire clock_1_out, not_1_out;

  Clock clock_1 (.out(clock_1_out));
  not not_1 (not_1_out, in_3);
  Counter counter_1 (.load(in_3), .D(in_2), .count(not_1_out), .clk(clock_1_out));  // open: Q, carry, clr
  ROM #(.dataWidth(21)) rom_1 (
    .addr(in_1),
    .data({out_5[9:8], out_4[9], out_4[10], out_4[11], out_5[10], out_5[11], out_5[5:4], out_4[5], out_4[6], out_4[7], out_5[6], out_5[7], out_5[1:0], out_4[1], out_4[2], out_4[3], out_5[2], out_5[3]}));  // open: sel
  _7_Segment_Display u_7_segment_display_1 (
    .g(out_5[11]), .f(out_5[10]), .a(out_5[9]), .b(out_5[8]), .e(out_4[11]), .d(out_4[10]), .c(out_4[9]),
    .dp(1'b0));
  _7_Segment_Display u_7_segment_display_2 (
    .g(out_5[7]), .f(out_5[6]), .a(out_5[5]), .b(out_5[4]), .e(out_4[7]), .d(out_4[6]), .c(out_4[5]),
    .dp(1'b0));
  _7_Segment_Display u_7_segment_display_3 (
    .g(out_5[3]), .f(out_5[2]), .a(out_5[1]), .b(out_5[0]), .e(out_4[3]), .d(out_4[2]), .c(out_4[1]),
    .dp(1'b0));

  assign {out_4[8], out_4[4], out_4[0]} = 3'b000;

  // Notes on the sheet:
  //   contents of rom_1 (hex, n*v repeats v):
  //   1fbf7e 1fbf30 1fbf6d 1fbf79 1fbf33 1fbf5b 1fbf5f 1fbf70 1fbf7f 1fbf7b 1f987e 1f9830 1f986d 1f9879
  //   1f9833 1f985b 1f985f 1f9870 1f987f 1f987b 1fb6fe 1fb6b0 1fb6ed 1fb6f9 1fb6b3 1fb6db 1fb6df 1fb6f0
  //   1fb6ff 1fb6fb 1fbcfe 1fbcb0 1fbced 1fbcf9 1fbcb3 1fbcdb 1fbcdf 1fbcf0 1fbcff 1fbcfb 1f99fe 1f99b0
  //   1f99ed 1f99f9 1f99b3 1f99db 1f99df 1f99f0 1f99ff 1f99fb 1fadfe 1fadb0 1faded 1fadf9 1fadb3 1faddb
  //   1faddf 1fadf0 1fadff 1fadfb 1faffe 1fafb0 1fafed 1faff9 1fafb3 1fafdb 1fafdf 1faff0 1fafff 1faffb
  //   1fb87e 1fb830 1fb86d 1fb879 1fb833 1fb85b 1fb85f 1fb870 1fb87f 1fb87b 1fbffe 1fbfb0 1fbfed 1fbff9
  //   1fbfb3 1fbfdb 1fbfdf 1fbff0 1fbfff 1fbffb 1fbdfe 1fbdb0 1fbded 1fbdf9 1fbdb3 1fbddb 1fbddf 1fbdf0
  //   1fbdff 1fbdfb c3f7e c3f30 c3f6d c3f79 c3f33 c3f5b c3f5f c3f70 c3f7f c3f7b c187e c1830 c186d c1879
  //   c1833 c185b c185f c1870 c187f c187b c36fe c36b0 c36ed c36f9 c36b3 c36db c36df c36f0 c36ff c36fb
  //   c3cfe c3cb0 c3ced c3cf9 c3cb3 c3cdb c3cdf c3cf0 c3cff c3cfb c19fe c19b0 c19ed c19f9 c19b3 c19db
  //   c19df c19f0 c19ff c19fb c2dfe c2db0 c2ded c2df9 c2db3 c2ddb c2ddf c2df0 c2dff c2dfb c2ffe c2fb0
  //   c2fed c2ff9 c2fb3 c2fdb c2fdf c2ff0 c2fff c2ffb c387e c3830 c386d c3879 c3833 c385b c385f c3870
  //   c387f c387b c3ffe c3fb0 c3fed c3ff9 c3fb3 c3fdb c3fdf c3ff0 c3fff c3ffb c3dfe c3db0 c3ded c3df9
  //   c3db3 c3ddb c3ddf c3df0 c3dff c3dfb 1b7f7e 1b7f30 1b7f6d 1b7f79 1b7f33 1b7f5b 1b7f5f 1b7f70 1b7f7f
  //   1b7f7b 1b587e 1b5830 1b586d 1b5879 1b5833 1b585b 1b585f 1b5870 1b587f 1b587b 1b76fe 1b76b0 1b76ed
  //   1b76f9 1b76b3 1b76db 1b76df 1b76f0 1b76ff 1b76fb 1b7cfe 1b7cb0 1b7ced 1b7cf9 1b7cb3 1b7cdb 1b7cdf
  //   1b7cf0 1b7cff 1b7cfb 1b59fe 1b59b0 1b59ed 1b59f9 1b59b3 1b59db 1b59df 1b59f0 1b59ff 1b59fb 1b6dfe
  //   1b6db0 1b6ded 1b6df9 1b6db3 1b6ddb
endmodule

module flag_bits_handler (
  input  CARRY,
  input  BORROW,
  input  EQUALS,
  input  GREATER,
  input  LESS,
  output [15:0] out_6
);


  assign out_6 = {{11{1'b0}}, LESS, GREATER, EQUALS, BORROW, CARRY};
endmodule

module InputFlagCombiner (
  input  [15:0] FlagsRegister,
  input  IF,
  output [15:0] out_3
);


  assign out_3 = {{10{1'b0}}, IF, FlagsRegister[4:0]};
endmodule

module HaltController (
  input  CLK,
  input  HLT,
  input  Run,
  output K
);

  wire and_1_out, d_ff_1_qn, or_1_out;

  D_Flip_Flop d_ff_1 (.clk(CLK), .D(Run), .Qn(d_ff_1_qn));  // open: Q, preset, en, reset
  and and_1 (and_1_out, d_ff_1_qn, Run);
  or or_1 (or_1_out, ~HLT, and_1_out);  // OR_Gate
  and and_2 (K, CLK, or_1_out);
endmodule
